# Fritzing sketch protoboard (saved by Fritzing 0.8.7b)
breadboards: 1

parts:
  Parte1 = Arduino Uno (Rev3)
  Parte2 = Triple Axis Accelerometer Breakout - ADXL335
  R2 = Resistor [tolerance=±5% resistance=1k package=THT]
  R3 = Resistor [tolerance=±5% resistance=1k package=THT]
  S1 = Pushbutton [package="[THT]"]
  C1 = Capacitor [package=cap-pth-large]

nets:
  N1: Parte1.A0, Parte2.XOUT
  N2: Parte1.A1, Parte2.YOUT
  N3: Parte1.A2, Parte2.ZOUT
  GND: Parte1.GND, Parte2.GND, S1.Pin_1, S1.Pin_2, C1.2
  N4: Parte1.AREF, R3.Pin_1
  N5: Parte1.D2, R2.Pin_0, S1.Pin_3, S1.Pin_4, C1.1
  3V3: Parte1.3V3, Parte2.VCC, R3.Pin_0
  N6: Parte1.5V, R2.Pin_1
