# Fritzing sketch protoboard (saved by Fritzing 0.8.7b)
breadboards: 1

parts:
  Parte1 = Arduino Uno (Rev3)
  R1 = Resistor [tolerance=±5% resistance=1k package=THT]
  R2 = Resistor [tolerance=±5% resistance=1k package=THT]
  LED1 = LED - 5mm [color="Red (633nm)" package="5 mm [THT]"]
  LED2 = LED - 5mm [color="Green (555nm)" package="5 mm [THT]"]
  R3 = Photocell (LDR) [package=THT]
  R5 = Resistor [tolerance=±5% resistance=68k package=THT]

nets:
  N1: Parte1.A0, R3.pin_1, R5.Pin_1
  N2: Parte1.D8, LED2.anode
  N3: Parte1.D9_PWM, LED1.anode
  N4: Parte1.5V, R5.Pin_0
  N5: Parte1.GND, R1.Pin_0, R2.Pin_0, R3.pin_0
  N6: R1.Pin_1, LED1.cathode
  N7: R2.Pin_1, LED2.cathode
