# Fritzing sketch protoboard (saved by Fritzing 0.6.3b)
breadboards: 1

parts:
  Arduino1 = Arduino
  LED1 = LED - 5mm [color="Red (633nm)" package="5 mm [THT]"]
  LED2 = LED - 5mm [color="Green (555nm)" package="5 mm [THT]"]
  R1 = Resistor [tolerance=±5% resistance=680 package=THT]
  R2 = Resistor [tolerance=±5% resistance=680 package=THT]
  R3 = Resistor [tolerance=±2% resistance=1k package=THT]
  R4 = Resistor [tolerance=±2% resistance=1k package=THT]
  S3 = Pushbutton [package="[THT]"]
  S4 = Pushbutton [package="[THT]"]

nets:
  N1: Arduino1.D9, LED1.anode
  N2: Arduino1.D8, LED2.anode
  N3: Arduino1.D3, R3.Pin_1, S3.Pin_3, S3.Pin_4
  N4: Arduino1.D2, R4.Pin_1, S4.Pin_3, S4.Pin_4
  N5: Arduino1.+5V, S3.Pin_1, S3.Pin_2, S4.Pin_1, S4.Pin_2
  N6: Arduino1.GND, R1.Pin_0, R2.Pin_0, R3.Pin_0, R4.Pin_0
  N7: LED1.cathode, R1.Pin_1
  N8: LED2.cathode, R2.Pin_1
