# Fritzing sketch protoboard (saved by Fritzing 0.8.7b)
breadboards: 1

parts:
  Parte1 = Arduino Uno (Rev3)
  R1 = Resistor [tolerance=±5% resistance=1k package=THT]
  R2 = Resistor [tolerance=±5% resistance=1k package=THT]
  LED3 = LED - 5mm [color="Red (633nm)" package="5 mm [THT]"]
  LED4 = LED - 5mm [color="Green (555nm)" package="5 mm [THT]"]
  R3 = Resistor [tolerance=±5% resistance=4.7k package=THT]
  R4 = Resistor [tolerance=±5% resistance=4.7k package=THT]
  S1 = Pushbutton [package=THT]
  S2 = Pushbutton [package=THT]

nets:
  N1: Parte1.D8, LED4.anode
  N2: Parte1.D9_PWM, LED3.anode
  N3: Parte1.D2, R4.Pin_1, S1.leg1
  N4: Parte1.D3_PWM, R3.Pin_1, S2.leg1
  N5: Parte1.5V, R3.Pin_0, R4.Pin_0
  N6: Parte1.GND, R1.Pin_0, R2.Pin_0, S1.leg0, S2.leg0
  N7: R1.Pin_1, LED3.cathode
  N8: R2.Pin_1, LED4.cathode
